# Fritzing sketch esquema_fritzing (saved by Fritzing 0.9.3b)
breadboards: 1

parts:
  S1 = Pushbutton [package="[THT]"]
  S2 = Pushbutton [package="[THT]"]
  S3 = Pushbutton [package="[THT]"]
  S4 = Pushbutton [package="[THT]"]
  S5 = Pushbutton [package="[THT]"]
  R1 = Resistor [tolerance=±5% resistance=10k package=THT]
  R2 = Resistor [tolerance=±5% resistance=10k package=THT]
  R3 = Resistor [tolerance=±5% resistance=10k package=THT]
  R4 = Resistor [tolerance=±5% resistance=10k package=THT]
  R5 = Resistor [tolerance=±5% resistance=10k package=THT]
  Raspberry_Pi_1 = Raspberry Pi 3 [part_number=RPI-3-V1.2]

nets:
  N1: S1.Pin_1, S1.Pin_2, S2.Pin_1, S2.Pin_2, S3.Pin_1, S3.Pin_2, S4.Pin_1, S4.Pin_2, S5.Pin_1, S5.Pin_2, Raspberry_Pi_1.3v3
  N2: S1.Pin_3, S1.Pin_4, R2.Pin_1
  N3: S2.Pin_3, S2.Pin_4, R1.Pin_1
  N4: S3.Pin_3, S3.Pin_4, R3.Pin_1
  N5: S4.Pin_3, S4.Pin_4, R4.Pin_1
  N6: S5.Pin_3, S5.Pin_4, R5.Pin_1
  N7: R1.Pin_0, Raspberry_Pi_1.GPIO17
  N8: R2.Pin_0, Raspberry_Pi_1.GPIO23
  N9: R3.Pin_0, Raspberry_Pi_1.GPIO27
  N10: R4.Pin_0, Raspberry_Pi_1.GPIO22
  N11: R5.Pin_0, Raspberry_Pi_1.GPIO18
